// Logisim project Sequential Decoder.circ as structural Verilog: 1 circuit, main circuit main
module main (
  output a,
  output b,
  output c,
  output d,
  output e,
  output f,
  output g
);

  wire and_1_out, ClK_out, decoder_1_out0, decoder_1_out1, decoder_1_out2, decoder_1_out3, decoder_1_out4,
       decoder_1_out5, decoder_1_out6, decoder_1_out7;
  wire [2:0] C_q;

  Clock ClK (.out(ClK_out));
  T_Flip_Flop u_A (.clk(ClK_out), .T(and_1_out), .Q(C_q[2]));  // open: Qn, preset, reset, en
  and and_1 (and_1_out, C_q[1], C_q[0]);
  T_Flip_Flop u_B (.clk(ClK_out), .T(C_q[0]), .Q(C_q[1]));  // open: Qn, preset, reset, en
  T_Flip_Flop u_C (.clk(ClK_out), .T(1'b1), .Q(C_q[0]));  // open: Qn, preset, reset, en
  Decoder #(.select(3)) decoder_1 (
    .out0(decoder_1_out0), .out1(decoder_1_out1), .out2(decoder_1_out2), .out3(decoder_1_out3),
    .out4(decoder_1_out4), .out5(decoder_1_out5), .out6(decoder_1_out6), .out7(decoder_1_out7), .sel(C_q));  // open: en
  or or_1 (d, decoder_1_out1, decoder_1_out3, decoder_1_out4, decoder_1_out7);
  or or_2 (e, decoder_1_out3, decoder_1_out7);
  or or_3 (f, decoder_1_out1, decoder_1_out6, decoder_1_out7);
  or or_4 (g, decoder_1_out1, decoder_1_out3, decoder_1_out4, decoder_1_out6);
  or or_5 (a, decoder_1_out1, decoder_1_out3, decoder_1_out4, decoder_1_out5, decoder_1_out7);
  or or_6 (c, decoder_1_out0, decoder_1_out1, decoder_1_out2, decoder_1_out4, decoder_1_out5, decoder_1_out6, decoder_1_out7);
  _7_Segment_Display u_7_segment_display_1 (.g(g), .f(f), .a(a), .b(1'b1), .e(e), .d(d), .c(c), .dp(1'b1));

  assign b = 1'b1;
endmodule
