// Logisim project Sequential Mux.circ as structural Verilog: 1 circuit, main circuit main
module main (
  output a,
  output b,
  output c,
  output d,
  output e,
  output f,
  output g
);

  wire and_1_out, C_q, ClK_out, not_1_out, not_2_out;
  wire [1:0] B_q;

  Clock ClK (.out(ClK_out));
  T_Flip_Flop u_A (.clk(ClK_out), .T(and_1_out), .Q(B_q[1]));  // open: Qn, preset, reset, en
  and and_1 (and_1_out, B_q[0], C_q);
  T_Flip_Flop u_B (.clk(ClK_out), .T(C_q), .Q(B_q[0]));  // open: Qn, preset, reset, en
  T_Flip_Flop u_C (.clk(ClK_out), .T(1'b1), .Q(C_q));  // open: Qn, preset, reset, en
  not not_1 (not_1_out, C_q);
  not not_2 (not_2_out, 1'b1);
  Multiplexer #(.select(2)) multiplexer_1 (
    .in0(C_q), .in1(C_q), .in2(1'b1), .in3(C_q), .out(a), .sel(B_q));  // open: en
  Multiplexer #(.select(2)) multiplexer_2 (
    .in0(1'b1), .in1(not_1_out), .in2(1'b1), .in3(1'b1), .out(c), .sel(B_q));  // open: en
  Multiplexer #(.select(2)) multiplexer_3 (
    .in0(C_q), .in1(C_q), .in2(not_1_out), .in3(C_q), .out(d), .sel(B_q));  // open: en
  Multiplexer #(.select(2)) multiplexer_4 (
    .in0(not_2_out), .in1(C_q), .in2(not_2_out), .in3(C_q), .out(e), .sel(B_q));  // open: en
  Multiplexer #(.select(2)) multiplexer_5 (
    .in0(C_q), .in1(not_2_out), .in2(not_2_out), .in3(1'b1), .out(f), .sel(B_q));  // open: en
  Multiplexer #(.select(2)) multiplexer_6 (
    .in0(C_q), .in1(C_q), .in2(not_1_out), .in3(not_1_out), .out(g), .sel(B_q));  // open: en
  _7_Segment_Display u_7_segment_display_1 (.g(g), .f(f), .a(a), .b(1'b1), .e(e), .d(d), .c(c), .dp(1'b1));

  assign b = 1'b1;

  // Notes on the sheet:
  //   C
  //   a
  //   c
  //   d
  //   e
  //   f
  //   g
endmodule
