// Logisim project Sequential Normal Gate.circ as structural Verilog: 1 circuit, main circuit main
module main (
  output a,
  output b,
  output c,
  output d,
  output e,
  output f,
  output g
);

  wire A_q, and_1_out, and_3_out, and_4_out, and_5_out, and_6_out, and_7_out, and_8_out, and_9_out,
       and_10_out, B_q, C_q, Clk_out, not_1_out, not_2_out, not_3_out, not_4_out, not_5_out, not_6_out,
       not_7_out, not_8_out, not_9_out, not_10_out;

  Clock Clk (.out(Clk_out));
  and and_1 (and_1_out, B_q, C_q);
  T_Flip_Flop u_A (.clk(Clk_out), .T(and_1_out), .Q(A_q));  // open: Qn, preset, reset, en
  T_Flip_Flop u_B (.clk(Clk_out), .T(C_q), .Q(B_q));  // open: Qn, preset, reset, en
  T_Flip_Flop u_C (.clk(Clk_out), .T(1'b1), .Q(C_q));  // open: Qn, preset, reset, en
  not not_1 (not_1_out, B_q);
  not not_2 (not_2_out, B_q);
  not not_3 (not_3_out, C_q);
  not not_4 (not_4_out, A_q);
  not not_5 (not_5_out, B_q);
  not not_6 (not_6_out, C_q);
  and and_2 (e, B_q, C_q);
  not not_7 (not_7_out, A_q);
  not not_8 (not_8_out, B_q);
  not not_9 (not_9_out, A_q);
  not not_10 (not_10_out, C_q);
  and and_3 (and_3_out, A_q, not_1_out);
  or or_1 (c, not_2_out, not_3_out, A_q);
  and and_4 (and_4_out, not_4_out, C_q);
  and and_5 (and_5_out, B_q, C_q);
  and and_6 (and_6_out, A_q, not_5_out, not_6_out);
  and and_7 (and_7_out, not_7_out, not_8_out, C_q);
  and and_8 (and_8_out, A_q, B_q);
  and and_9 (and_9_out, not_9_out, C_q);
  and and_10 (and_10_out, A_q, not_10_out);
  or or_2 (a, C_q, and_3_out);
  or or_3 (d, and_4_out, and_5_out, and_6_out);
  or or_4 (f, and_7_out, and_8_out);
  or or_5 (g, and_9_out, and_10_out);
  _7_Segment_Display u_7_segment_display_1 (.g(g), .f(f), .a(a), .b(1'b1), .e(e), .d(d), .c(c), .dp(1'b1));

  assign b = 1'b1;
endmodule
