// Logisim project Sequential Universal Gate.circ as structural Verilog: 1 circuit, main circuit main
module main (
  output a,
  output b,
  output c,
  output d,
  output e,
  output f,
  output g
);

  wire A_q, and_1_out, B_q, C_q, ClK_out, nand_1_out, nand_2_out, nand_3_out, nand_4_out, nand_5_out,
       nand_6_out, nand_7_out, nand_8_out, nand_9_out, nand_10_out, nand_11_out, nand_12_out, nand_14_out,
       nand_15_out, nand_16_out, nand_18_out, nand_19_out, nand_20_out, nand_21_out;

  Clock ClK (.out(ClK_out));
  T_Flip_Flop u_A (.clk(ClK_out), .T(and_1_out), .Q(A_q));  // open: Qn, preset, reset, en
  and and_1 (and_1_out, B_q, C_q);
  T_Flip_Flop u_B (.clk(ClK_out), .T(C_q), .Q(B_q));  // open: Qn, preset, reset, en
  T_Flip_Flop u_C (.clk(ClK_out), .T(1'b1), .Q(C_q));  // open: Qn, preset, reset, en
  nand nand_1 (nand_1_out, B_q, B_q);
  nand nand_2 (nand_2_out, A_q, A_q);
  nand nand_3 (nand_3_out, A_q, A_q);
  nand nand_4 (nand_4_out, B_q, B_q);
  nand nand_5 (nand_5_out, C_q, C_q);
  nand nand_6 (nand_6_out, B_q, C_q);
  nand nand_7 (nand_7_out, A_q, A_q);
  nand nand_8 (nand_8_out, B_q, B_q);
  nand nand_9 (nand_9_out, A_q, A_q);
  nand nand_10 (nand_10_out, C_q, C_q);
  nand nand_11 (nand_11_out, C_q, C_q);
  nand nand_12 (nand_12_out, A_q, nand_1_out);
  nand nand_13 (c, B_q, C_q, nand_2_out);
  nand nand_14 (nand_14_out, nand_3_out, C_q);
  nand nand_15 (nand_15_out, B_q, C_q);
  nand nand_16 (nand_16_out, A_q, nand_4_out, nand_5_out);
  nand nand_17 (e, nand_6_out, nand_6_out);
  nand nand_18 (nand_18_out, nand_7_out, nand_8_out, C_q);
  nand nand_19 (nand_19_out, A_q, B_q);
  nand nand_20 (nand_20_out, nand_9_out, C_q);
  nand nand_21 (nand_21_out, A_q, nand_10_out);
  nand nand_22 (a, nand_11_out, nand_12_out);
  nand nand_23 (d, nand_14_out, nand_15_out, nand_16_out);
  nand nand_24 (f, nand_18_out, nand_19_out);
  nand nand_25 (g, nand_20_out, nand_21_out);
  _7_Segment_Display u_7_segment_display_1 (.g(g), .f(f), .a(a), .b(1'b1), .e(e), .d(d), .c(c), .dp(1'b1));

  assign b = 1'b1;
endmodule
