// Logisim project SqCk_7sementProject.circ as structural Verilog: 9 circuits, main circuit Normal Gates
module main (
);

  wire A_q, A_qn, and_1_out, B_q, B_qn, C_q, C_qn, CLK_out;

  Clock CLK (.out(CLK_out));
  T_Flip_Flop A (.clk(CLK_out), .T(and_1_out), .Q(A_q), .Qn(A_qn));  // open: preset, reset, en
  and and_1 (and_1_out, B_q, C_q);
  T_Flip_Flop B (.clk(CLK_out), .T(C_q), .Q(B_q), .Qn(B_qn));  // open: preset, reset, en
  T_Flip_Flop C (.clk(CLK_out), .T(1'b1), .Q(C_q), .Qn(C_qn));  // open: preset, reset, en
endmodule

module Normal_Gates (
  input  A,
  input  B,
  input  C,
  output a_2,
  output b_2,
  output c_2,
  output d,
  output e,
  output f,
  output g
);

  wire and_1_out, and_2_out, and_3_out, and_4_out, and_6_out, and_7_out, and_8_out, and_9_out, not_1_out,
       not_2_out, not_3_out, not_4_out, not_5_out, not_6_out, not_7_out, not_8_out, not_9_out, not_10_out;

  not not_1 (not_1_out, B);
  not not_2 (not_2_out, B);
  not not_3 (not_3_out, C);
  not not_4 (not_4_out, A);
  not not_5 (not_5_out, B);
  not not_6 (not_6_out, C);
  not not_7 (not_7_out, A);
  not not_8 (not_8_out, B);
  not not_9 (not_9_out, A);
  not not_10 (not_10_out, C);
  and and_1 (and_1_out, A, not_1_out);
  or or_1 (c_2, not_2_out, not_3_out, A);
  and and_2 (and_2_out, not_4_out, C);
  and and_3 (and_3_out, B, C);
  and and_4 (and_4_out, A, not_5_out, not_6_out);
  and and_5 (e, B, C);
  and and_6 (and_6_out, not_7_out, not_8_out, C);
  and and_7 (and_7_out, A, B);
  and and_8 (and_8_out, not_9_out, C);
  and and_9 (and_9_out, A, not_10_out);
  or or_2 (a_2, C, and_1_out);
  or or_3 (d, and_2_out, and_3_out, and_4_out);
  or or_4 (f, and_6_out, and_7_out);
  or or_5 (g, and_8_out, and_9_out);
  _7_Segment_Display u_7_segment_display_1 (.g(g), .f(f), .a(a_2), .b(1'b1), .e(e), .d(d), .c(c_2), .dp(1'b1));

  assign b_2 = 1'b1;
endmodule

module Universal_Gates (
  input  A,
  input  B,
  input  C,
  output a_2,
  output b_2,
  output c_2,
  output d,
  output e,
  output f,
  output g
);

  wire nand_1_out, nand_2_out, nand_3_out, nand_4_out, nand_5_out, nand_6_out, nand_7_out, nand_8_out,
       nand_9_out, nand_10_out, nand_11_out, nand_12_out, nand_14_out, nand_15_out, nand_16_out, nand_18_out,
       nand_19_out, nand_20_out, nand_21_out;

  nand nand_1 (nand_1_out, B, B);
  nand nand_2 (nand_2_out, A, A);
  nand nand_3 (nand_3_out, A, A);
  nand nand_4 (nand_4_out, B, B);
  nand nand_5 (nand_5_out, C, C);
  nand nand_6 (nand_6_out, B, C);
  nand nand_7 (nand_7_out, A, A);
  nand nand_8 (nand_8_out, B, B);
  nand nand_9 (nand_9_out, A, A);
  nand nand_10 (nand_10_out, C, C);
  nand nand_11 (nand_11_out, C, C);
  nand nand_12 (nand_12_out, A, nand_1_out);
  nand nand_13 (c_2, B, C, nand_2_out);
  nand nand_14 (nand_14_out, nand_3_out, C);
  nand nand_15 (nand_15_out, B, C);
  nand nand_16 (nand_16_out, A, nand_4_out, nand_5_out);
  nand nand_17 (e, nand_6_out, nand_6_out);
  nand nand_18 (nand_18_out, nand_7_out, nand_8_out, C);
  nand nand_19 (nand_19_out, A, B);
  nand nand_20 (nand_20_out, nand_9_out, C);
  nand nand_21 (nand_21_out, A, nand_10_out);
  nand nand_22 (a_2, nand_11_out, nand_12_out);
  nand nand_23 (d, nand_14_out, nand_15_out, nand_16_out);
  nand nand_24 (f, nand_18_out, nand_19_out);
  nand nand_25 (g, nand_20_out, nand_21_out);
  _7_Segment_Display u_7_segment_display_1 (.g(g), .f(f), .a(a_2), .b(1'b1), .e(e), .d(d), .c(c_2), .dp(1'b1));

  assign b_2 = 1'b1;
endmodule

module Decoder (
  input  A,
  input  B,
  input  C,
  output a_2,
  output b_2,
  output c_2,
  output d,
  output e,
  output f,
  output g
);

  wire decoder_1_out0, decoder_1_out1, decoder_1_out2, decoder_1_out3, decoder_1_out4, decoder_1_out5,
       decoder_1_out6, decoder_1_out7;

  Decoder_part #(.select(3)) decoder_1 (
    .out0(decoder_1_out0), .out1(decoder_1_out1), .out2(decoder_1_out2), .out3(decoder_1_out3),
    .out4(decoder_1_out4), .out5(decoder_1_out5), .out6(decoder_1_out6), .out7(decoder_1_out7),
    .sel({A, B, C}));  // open: en
  or or_1 (d, decoder_1_out1, decoder_1_out3, decoder_1_out4, decoder_1_out7);
  or or_2 (e, decoder_1_out3, decoder_1_out7);
  or or_3 (f, decoder_1_out1, decoder_1_out6, decoder_1_out7);
  or or_4 (g, decoder_1_out1, decoder_1_out3, decoder_1_out4, decoder_1_out6);
  or or_5 (a_2, decoder_1_out1, decoder_1_out3, decoder_1_out4, decoder_1_out5, decoder_1_out7);
  or or_6 (c_2, decoder_1_out0, decoder_1_out1, decoder_1_out2, decoder_1_out4, decoder_1_out5, decoder_1_out6, decoder_1_out7);
  _7_Segment_Display u_7_segment_display_1 (.g(g), .f(f), .a(a_2), .b(1'b1), .e(e), .d(d), .c(c_2), .dp(1'b1));

  assign b_2 = 1'b1;

  // Notes on the sheet:
  //   a
  //   c
  //   d
  //   e
  //   f
  //   g
endmodule

module MUX (
  input  A,
  input  B,
  input  C,
  output a_2,
  output b_2,
  output c_2,
  output d,
  output e,
  output f,
  output g
);

  wire not_1_out, not_2_out;

  not not_1 (not_1_out, C);
  not not_2 (not_2_out, 1'b1);
  Multiplexer #(.select(2)) multiplexer_1 (.in0(C), .in1(C), .in2(1'b1), .in3(C), .out(a_2), .sel({A, B}));  // open: en
  Multiplexer #(.select(2)) multiplexer_2 (
    .in0(1'b1), .in1(not_1_out), .in2(1'b1), .in3(1'b1), .out(c_2), .sel({A, B}));  // open: en
  Multiplexer #(.select(2)) multiplexer_3 (
    .in0(C), .in1(C), .in2(not_1_out), .in3(C), .out(d), .sel({A, B}));  // open: en
  Multiplexer #(.select(2)) multiplexer_4 (
    .in0(not_2_out), .in1(C), .in2(not_2_out), .in3(C), .out(e), .sel({A, B}));  // open: en
  Multiplexer #(.select(2)) multiplexer_5 (
    .in0(C), .in1(not_2_out), .in2(not_2_out), .in3(1'b1), .out(f), .sel({A, B}));  // open: en
  Multiplexer #(.select(2)) multiplexer_6 (
    .in0(C), .in1(C), .in2(not_1_out), .in3(not_1_out), .out(g), .sel({A, B}));  // open: en
  _7_Segment_Display u_7_segment_display_1 (.g(g), .f(f), .a(a_2), .b(1'b1), .e(e), .d(d), .c(c_2), .dp(1'b1));

  assign b_2 = 1'b1;
endmodule

module Sq_Normal_Gates (
  output a,
  output b,
  output c,
  output d,
  output e,
  output f,
  output g
);

  wire A_q, and_1_out, and_3_out, and_4_out, and_5_out, and_6_out, and_7_out, and_8_out, and_9_out,
       and_10_out, B_q, C_q, Clk_out, not_1_out, not_2_out, not_3_out, not_4_out, not_5_out, not_6_out,
       not_7_out, not_8_out, not_9_out, not_10_out;

  Clock Clk (.out(Clk_out));
  and and_1 (and_1_out, B_q, C_q);
  T_Flip_Flop u_A (.clk(Clk_out), .T(and_1_out), .Q(A_q));  // open: Qn, preset, reset, en
  T_Flip_Flop u_B (.clk(Clk_out), .T(C_q), .Q(B_q));  // open: Qn, preset, reset, en
  T_Flip_Flop u_C (.clk(Clk_out), .T(1'b1), .Q(C_q));  // open: Qn, preset, reset, en
  not not_1 (not_1_out, B_q);
  not not_2 (not_2_out, B_q);
  not not_3 (not_3_out, C_q);
  not not_4 (not_4_out, A_q);
  not not_5 (not_5_out, B_q);
  not not_6 (not_6_out, C_q);
  and and_2 (e, B_q, C_q);
  not not_7 (not_7_out, A_q);
  not not_8 (not_8_out, B_q);
  not not_9 (not_9_out, A_q);
  not not_10 (not_10_out, C_q);
  and and_3 (and_3_out, A_q, not_1_out);
  or or_1 (c, not_2_out, not_3_out, A_q);
  and and_4 (and_4_out, not_4_out, C_q);
  and and_5 (and_5_out, B_q, C_q);
  and and_6 (and_6_out, A_q, not_5_out, not_6_out);
  and and_7 (and_7_out, not_7_out, not_8_out, C_q);
  and and_8 (and_8_out, A_q, B_q);
  and and_9 (and_9_out, not_9_out, C_q);
  and and_10 (and_10_out, A_q, not_10_out);
  or or_2 (a, C_q, and_3_out);
  or or_3 (d, and_4_out, and_5_out, and_6_out);
  or or_4 (f, and_7_out, and_8_out);
  or or_5 (g, and_9_out, and_10_out);
  _7_Segment_Display u_7_segment_display_1 (.g(g), .f(f), .a(a), .b(1'b1), .e(e), .d(d), .c(c), .dp(1'b1));

  assign b = 1'b1;
endmodule

module Sq_Universal_Gates (
  output a,
  output b,
  output c,
  output d,
  output e,
  output f,
  output g
);

  wire A_q, and_1_out, B_q, C_q, ClK_out, nand_1_out, nand_2_out, nand_3_out, nand_4_out, nand_5_out,
       nand_6_out, nand_7_out, nand_8_out, nand_9_out, nand_10_out, nand_11_out, nand_12_out, nand_14_out,
       nand_15_out, nand_16_out, nand_18_out, nand_19_out, nand_20_out, nand_21_out;

  Clock ClK (.out(ClK_out));
  T_Flip_Flop u_A (.clk(ClK_out), .T(and_1_out), .Q(A_q));  // open: Qn, preset, reset, en
  and and_1 (and_1_out, B_q, C_q);
  T_Flip_Flop u_B (.clk(ClK_out), .T(C_q), .Q(B_q));  // open: Qn, preset, reset, en
  T_Flip_Flop u_C (.clk(ClK_out), .T(1'b1), .Q(C_q));  // open: Qn, preset, reset, en
  nand nand_1 (nand_1_out, B_q, B_q);
  nand nand_2 (nand_2_out, A_q, A_q);
  nand nand_3 (nand_3_out, A_q, A_q);
  nand nand_4 (nand_4_out, B_q, B_q);
  nand nand_5 (nand_5_out, C_q, C_q);
  nand nand_6 (nand_6_out, B_q, C_q);
  nand nand_7 (nand_7_out, A_q, A_q);
  nand nand_8 (nand_8_out, B_q, B_q);
  nand nand_9 (nand_9_out, A_q, A_q);
  nand nand_10 (nand_10_out, C_q, C_q);
  nand nand_11 (nand_11_out, C_q, C_q);
  nand nand_12 (nand_12_out, A_q, nand_1_out);
  nand nand_13 (c, B_q, C_q, nand_2_out);
  nand nand_14 (nand_14_out, nand_3_out, C_q);
  nand nand_15 (nand_15_out, B_q, C_q);
  nand nand_16 (nand_16_out, A_q, nand_4_out, nand_5_out);
  nand nand_17 (e, nand_6_out, nand_6_out);
  nand nand_18 (nand_18_out, nand_7_out, nand_8_out, C_q);
  nand nand_19 (nand_19_out, A_q, B_q);
  nand nand_20 (nand_20_out, nand_9_out, C_q);
  nand nand_21 (nand_21_out, A_q, nand_10_out);
  nand nand_22 (a, nand_11_out, nand_12_out);
  nand nand_23 (d, nand_14_out, nand_15_out, nand_16_out);
  nand nand_24 (f, nand_18_out, nand_19_out);
  nand nand_25 (g, nand_20_out, nand_21_out);
  _7_Segment_Display u_7_segment_display_1 (.g(g), .f(f), .a(a), .b(1'b1), .e(e), .d(d), .c(c), .dp(1'b1));

  assign b = 1'b1;
endmodule

module Sq_Decoder (
  output a,
  output b,
  output c,
  output d,
  output e,
  output f,
  output g
);

  wire and_1_out, ClK_out, decoder_1_out0, decoder_1_out1, decoder_1_out2, decoder_1_out3, decoder_1_out4,
       decoder_1_out5, decoder_1_out6, decoder_1_out7;
  wire [2:0] C_q;

  Clock ClK (.out(ClK_out));
  T_Flip_Flop u_A (.clk(ClK_out), .T(and_1_out), .Q(C_q[2]));  // open: Qn, preset, reset, en
  and and_1 (and_1_out, C_q[1], C_q[0]);
  T_Flip_Flop u_B (.clk(ClK_out), .T(C_q[0]), .Q(C_q[1]));  // open: Qn, preset, reset, en
  T_Flip_Flop u_C (.clk(ClK_out), .T(1'b1), .Q(C_q[0]));  // open: Qn, preset, reset, en
  Decoder_part #(.select(3)) decoder_1 (
    .out0(decoder_1_out0), .out1(decoder_1_out1), .out2(decoder_1_out2), .out3(decoder_1_out3),
    .out4(decoder_1_out4), .out5(decoder_1_out5), .out6(decoder_1_out6), .out7(decoder_1_out7), .sel(C_q));  // open: en
  or or_1 (d, decoder_1_out1, decoder_1_out3, decoder_1_out4, decoder_1_out7);
  or or_2 (e, decoder_1_out3, decoder_1_out7);
  or or_3 (f, decoder_1_out1, decoder_1_out6, decoder_1_out7);
  or or_4 (g, decoder_1_out1, decoder_1_out3, decoder_1_out4, decoder_1_out6);
  or or_5 (a, decoder_1_out1, decoder_1_out3, decoder_1_out4, decoder_1_out5, decoder_1_out7);
  or or_6 (c, decoder_1_out0, decoder_1_out1, decoder_1_out2, decoder_1_out4, decoder_1_out5, decoder_1_out6, decoder_1_out7);
  _7_Segment_Display u_7_segment_display_1 (.g(g), .f(f), .a(a), .b(1'b1), .e(e), .d(d), .c(c), .dp(1'b1));

  assign b = 1'b1;
endmodule

module Sq_MUX (
  output a,
  output b,
  output c,
  output d,
  output e,
  output f,
  output g
);

  wire and_1_out, C_q, ClK_out, not_1_out, not_2_out;
  wire [1:0] B_q;

  Clock ClK (.out(ClK_out));
  T_Flip_Flop u_A (.clk(ClK_out), .T(and_1_out), .Q(B_q[1]));  // open: Qn, preset, reset, en
  and and_1 (and_1_out, B_q[0], C_q);
  T_Flip_Flop u_B (.clk(ClK_out), .T(C_q), .Q(B_q[0]));  // open: Qn, preset, reset, en
  T_Flip_Flop u_C (.clk(ClK_out), .T(1'b1), .Q(C_q));  // open: Qn, preset, reset, en
  not not_1 (not_1_out, C_q);
  not not_2 (not_2_out, 1'b1);
  Multiplexer #(.select(2)) multiplexer_1 (
    .in0(C_q), .in1(C_q), .in2(1'b1), .in3(C_q), .out(a), .sel(B_q));  // open: en
  Multiplexer #(.select(2)) multiplexer_2 (
    .in0(1'b1), .in1(not_1_out), .in2(1'b1), .in3(1'b1), .out(c), .sel(B_q));  // open: en
  Multiplexer #(.select(2)) multiplexer_3 (
    .in0(C_q), .in1(C_q), .in2(not_1_out), .in3(C_q), .out(d), .sel(B_q));  // open: en
  Multiplexer #(.select(2)) multiplexer_4 (
    .in0(not_2_out), .in1(C_q), .in2(not_2_out), .in3(C_q), .out(e), .sel(B_q));  // open: en
  Multiplexer #(.select(2)) multiplexer_5 (
    .in0(C_q), .in1(not_2_out), .in2(not_2_out), .in3(1'b1), .out(f), .sel(B_q));  // open: en
  Multiplexer #(.select(2)) multiplexer_6 (
    .in0(C_q), .in1(C_q), .in2(not_1_out), .in3(not_1_out), .out(g), .sel(B_q));  // open: en
  _7_Segment_Display u_7_segment_display_1 (.g(g), .f(f), .a(a), .b(1'b1), .e(e), .d(d), .c(c), .dp(1'b1));

  assign b = 1'b1;

  // Notes on the sheet:
  //   C
  //   a
  //   c
  //   d
  //   e
  //   f
  //   g
endmodule
